# Fritzing sketch ReactionMeasurement (saved by Fritzing 1.0.4)
breadboards: 1

parts:
  Part1 = Arduino Uno (Rev3)
  S1 = Pushbutton [package="[THT]"]
  S2 = Pushbutton [package="[THT]"]
  S3 = Pushbutton [package="[THT]"]
  LED1 = LED - 5mm [color="Red (633nm)" current=0.030A package="5 mm [THT]"]
  LED2 = LED - 5mm [color="Green (555nm)" current=0.030A package="5 mm [THT]"]
  R1 = Resistor [tolerance=±5% power=0.25W resistance=220 package=THT]
  LED3 = LED - 5mm [color="Blue (470nm)" current=0.030A package="5 mm [THT]"]
  R2 = Resistor [tolerance=±5% power=0.25W resistance=220 package=THT]
  R3 = Resistor [tolerance=±5% power=0.25W resistance=220 package=THT]
  R4 = Resistor [tolerance=±5% power=0.25W resistance=10k package=THT]
  Buzzer = Passive Buzzer

nets:
  N1: Part1.D8, R4.Pin_0
  N2: Part1.D2, LED1.anode
  N3: Part1.D3_PWM, LED2.anode
  N4: Part1.D4, LED3.anode
  N5: Part1.D5_PWM, S3.Pin_3, S3.Pin_4
  N6: Part1.D6_PWM, S2.Pin_3, S2.Pin_4
  N7: Part1.D7, S1.Pin_3, S1.Pin_4
  N8: Part1.5V, Buzzer.-
  N9: Part1.GND, S1.Pin_1, S2.Pin_1, S3.Pin_1, R1.Pin_0, R2.Pin_0, R3.Pin_0, Buzzer.S
  N10: LED1.cathode, R1.Pin_1
  N11: LED2.cathode, R2.Pin_1
  N12: LED3.cathode, R3.Pin_1
  N13: R4.Pin_1, Buzzer.NC

notes:
  VCC
  GND
  I/O
  R1
  C1
  R2
  R3
  C3
  C2
