# Fritzing sketch SquareWaveSwitchLED (saved by Fritzing 1.0.4)
breadboards: 1

parts:
  Part1 = Real Time Clock Module - DS1307 RTC Breakout Board
  Part2 = Arduino Uno (Rev3)
  R1 = Resistor [tolerance=±5% power=0.25W resistance=220 package=THT]
  LED1 = LED - 5mm [color="Red (633nm)" current=0.030A package="5 mm [THT]"]
  Mod1 = Passive Buzzer

nets:
  N1: Part1.5V, Mod1.S
  N2: Part1.GND, LED1.cathode, Mod1.-
  N3: Part1.SQW, Part2.D2
  N4: Part1.SCL, Part2.A5/SCL
  N5: Part1.SDA, Part2.A4/SDA
  N6: Part2.D8, R1.Pin_1
  N7: Part2.D9_PWM, Mod1.NC
  N8: R1.Pin_0, LED1.anode

notes:
  GND
  VCC
  I/O
