# Fritzing sketch AndGateButton (saved by Fritzing 1.0.4)
breadboards: 1

parts:
  Part1 = Arduino Uno (Rev3)
  S1 = Momentary Switch [package=ksa_sealed_tac_switch]
  S2 = Momentary Switch [package=ksa_sealed_tac_switch]
  LED1 = LED - 5mm [color="Red (633nm)" current=0.030A package="5 mm [THT]"]
  R1 = Resistor [tolerance=±5% power=0.25W resistance=220 package=THT]

nets:
  N1: Part1.GND, LED1.cathode
  N2: Part1.5V, S1.2
  N3: S1.3, S2.2
  N4: S2.3, R1.Pin_1
  N5: LED1.anode, R1.Pin_0

notes:
  R1
  C1
  R2
  C2
