# Fritzing sketch Oscillator (saved by Fritzing 1.0.4)
breadboards: 1

parts:
  Part1 = Arduino Uno (Rev3)
  Q1 = NPN-Transistor [package="TO92 [THT]"]
  Q2 = NPN-Transistor [package="TO92 [THT]"]
  C1 = Electrolytic Capacitor [capacitance=10µF voltage=35V package="1010 [SMD, electrolytic]"]
  LED1 = LED - 5mm [color="Red (633nm)" current=0.030A package="5 mm [THT]"]
  R1 = Resistor [tolerance=±5% power=0.25W resistance=220 package=THT]
  U1 = SLIDER [knob_status=50% power=0.5W package=slider]
  C2 = Electrolytic Capacitor [capacitance=10µF voltage=35V package="1010 [SMD, electrolytic]"]
  R2 = Resistor [tolerance=±5% power=0.25W resistance=1k package=THT]
  R3 = Resistor [tolerance=±5% power=0.25W resistance=10k package=THT]
  R4 = Resistor [tolerance=±5% power=0.25W resistance=10k package=THT]

nets:
  N1: Part1.5V, R1.Pin_1, U1.S, R2.Pin_1
  N2: Part1.GND, Q1.E, Q2.E
  N3: Q1.B, C1.-, R4.Pin_1
  N4: Q1.C, C2.-, R2.Pin_0
  N5: Q2.B, R3.Pin_1
  N6: Q2.C, C1.+, LED1.cathode
  N7: LED1.anode, R1.Pin_0
  N8: U1.E, C2.+, R3.Pin_0

notes:
  OTA
  VCC
